// Logisim project UAL.circ as structural Verilog: 4 circuits, main circuit main
module main (
  input  [7:0] rs,
  input  [7:0] rt,
  input  [7:0] halt,
  input  [2:0] in_4,
  output [3:0] Flags,
  output [7:0] out_6
);

  wire adder_1_cout, and_1_out, and_2_out, and_4_out, and_5_out, and_6_out, and_7_out, and_8_out, and_9_out,
       and_10_out, and_11_out, and_12_out, or_2_out, or_3_out, subtractor_1_bout;
  wire [7:0] adder_1_out, and_3_out, not_1_out, or_1_out, shifter_1_out, shifter_2_out, subtractor_1_out;

  and and_1 (and_1_out, ~rs[7], ~rt[7]);  // AND_Gate
  and and_2 (and_2_out, rs[7], rt[7]);
  Adder adder_1 (.a(rs), .b(rt), .out(adder_1_out), .cout(adder_1_cout));  // open: cin
  Subtractor subtractor_1 (.a(rs), .b(rt), .out(subtractor_1_out), .bout(subtractor_1_bout));  // open: bin
  assign or_1_out = rs | rt;  // OR_Gate or_1, 8 bits wide
  assign and_3_out = rs & rt;  // AND_Gate and_3, 8 bits wide
  assign not_1_out = ~rs;  // NOT_Gate not_1, 8 bits wide
  Shifter shifter_1 (.in(rs), .\dist (rt[2:0]), .out(shifter_1_out));
  Shifter #(.shift("lr")) shifter_2 (.in(rs), .\dist (rt[2:0]), .out(shifter_2_out));
  and and_4 (and_4_out, and_1_out, adder_1_out[7]);
  or or_2 (or_2_out, and_2_out, and_1_out);
  and and_5 (and_5_out, and_2_out, ~adder_1_out[7]);  // AND_Gate
  or or_3 (or_3_out, and_4_out, and_5_out);
  and and_6 (and_6_out, subtractor_1_out[7], or_2_out);
  and and_7 (and_7_out, and_6_out, and_10_out);
  Multiplexer #(.select(3), .width(8)) multiplexer_1 (
    .in0(halt), .in1(adder_1_out), .in2(subtractor_1_out), .in3(or_1_out), .in4(and_3_out), .in5(not_1_out),
    .in6(shifter_1_out), .in7(shifter_2_out), .out({Flags[2], out_6[6:0]}), .sel(in_4));  // open: en
  or or_4 (Flags[3], and_7_out, and_8_out);
  and and_8 (and_8_out, and_9_out, or_3_out);
  nor nor_1 (Flags[1], out_6[0], out_6[1], out_6[2], out_6[3], out_6[4], out_6[5], out_6[6], Flags[2]);
  and and_9 (and_9_out, in_4[0], ~in_4[1], ~in_4[2]);  // AND_Gate
  and and_10 (and_10_out, ~in_4[0], in_4[1], ~in_4[2]);  // AND_Gate
  or or_5 (Flags[0], and_11_out, and_12_out);
  and and_11 (and_11_out, adder_1_cout, and_9_out);
  and and_12 (and_12_out, subtractor_1_bout, and_10_out);

  assign out_6[7] = Flags[2];

  // Notes on the sheet:
  //   OF pour sub
  //   OF pour l'addition
  //   ZF
  //   osef de sa valeur
  //   code add
  //   code sub
  //   OP code add
  //   OF
  //   SF
  //   CF add
  //   Of SF ZF CF
  //   CF sub
endmodule

module UAL (
  input  [7:0] rs,
  input  [7:0] rt,
  input  [7:0] halt,
  input  [2:0] in_4,
  output [3:0] Flags,
  output [7:0] out_6
);

  wire adder_1_cout, and_1_out, and_2_out, and_4_out, and_5_out, and_6_out, and_7_out, and_8_out, and_9_out,
       and_10_out, and_11_out, and_12_out, or_2_out, or_3_out, subtractor_1_bout;
  wire [7:0] adder_1_out, and_3_out, not_1_out, or_1_out, shifter_1_out, shifter_2_out, subtractor_1_out;

  and and_1 (and_1_out, ~rs[7], ~rt[7]);  // AND_Gate
  and and_2 (and_2_out, rs[7], rt[7]);
  Adder adder_1 (.a(rs), .b(rt), .out(adder_1_out), .cout(adder_1_cout));  // open: cin
  Subtractor subtractor_1 (.a(rs), .b(rt), .out(subtractor_1_out), .bout(subtractor_1_bout));  // open: bin
  assign or_1_out = rs | rt;  // OR_Gate or_1, 8 bits wide
  assign and_3_out = rs & rt;  // AND_Gate and_3, 8 bits wide
  assign not_1_out = ~rs;  // NOT_Gate not_1, 8 bits wide
  Shifter shifter_1 (.in(rs), .\dist (rt[2:0]), .out(shifter_1_out));
  Shifter #(.shift("lr")) shifter_2 (.in(rs), .\dist (rt[2:0]), .out(shifter_2_out));
  and and_4 (and_4_out, and_1_out, adder_1_out[7]);
  or or_2 (or_2_out, and_2_out, and_1_out);
  and and_5 (and_5_out, and_2_out, ~adder_1_out[7]);  // AND_Gate
  or or_3 (or_3_out, and_4_out, and_5_out);
  and and_6 (and_6_out, subtractor_1_out[7], or_2_out);
  and and_7 (and_7_out, and_6_out, and_10_out);
  Multiplexer #(.select(3), .width(8)) multiplexer_1 (
    .in0(halt), .in1(adder_1_out), .in2(subtractor_1_out), .in3(or_1_out), .in4(and_3_out), .in5(not_1_out),
    .in6(shifter_1_out), .in7(shifter_2_out), .out({Flags[2], out_6[6:0]}), .sel(in_4));  // open: en
  or or_4 (Flags[3], and_7_out, and_8_out);
  and and_8 (and_8_out, and_9_out, or_3_out);
  nor nor_1 (Flags[1], out_6[0], out_6[1], out_6[2], out_6[3], out_6[4], out_6[5], out_6[6], Flags[2]);
  and and_9 (and_9_out, in_4[0], ~in_4[1], ~in_4[2]);  // AND_Gate
  and and_10 (and_10_out, ~in_4[0], in_4[1], ~in_4[2]);  // AND_Gate
  or or_5 (Flags[0], and_11_out, and_12_out);
  and and_11 (and_11_out, adder_1_cout, and_9_out);
  and and_12 (and_12_out, subtractor_1_bout, and_10_out);

  assign out_6[7] = Flags[2];

  // Notes on the sheet:
  //   OF pour sub
  //   OF pour l'addition
  //   ZF
  //   osef de sa valeur
  //   code add
  //   code sub
  //   OP code add
  //   OF
  //   SF
  //   CF add
  //   Of SF ZF CF
  //   CF sub
endmodule

module BancDeRegistres (
  input  [3:0] Selc_rt,
  input  [7:0] valln,
  input  Reset,
  input  [3:0] Selec_rd,
  input  [3:0] Selec_rs,
  input  InputClock,
  input  regW,
  output [7:0] Rt,
  output [7:0] Rs
);

  wire clock_1_out, demultiplexer_2_out0, demultiplexer_2_out1, demultiplexer_2_out2, demultiplexer_2_out3,
       demultiplexer_2_out4, demultiplexer_2_out5, demultiplexer_2_out6, demultiplexer_2_out7,
       demultiplexer_2_out8, demultiplexer_2_out9, demultiplexer_2_out10, demultiplexer_2_out11,
       demultiplexer_2_out12, demultiplexer_2_out13, demultiplexer_2_out14, demultiplexer_2_out15;
  wire [7:0] demultiplexer_1_out0, demultiplexer_1_out1, demultiplexer_1_out2, demultiplexer_1_out3,
       demultiplexer_1_out4, demultiplexer_1_out5, demultiplexer_1_out6, demultiplexer_1_out7,
       demultiplexer_1_out8, demultiplexer_1_out9, demultiplexer_1_out10, demultiplexer_1_out11,
       demultiplexer_1_out12, demultiplexer_1_out13, demultiplexer_1_out14, demultiplexer_1_out15, R1, R2,
       R3, R4, R5, R6, R7, R8, R9, R10, R11, R12, R13, R14, R15, R16;

  Clock clock_1 (.out(clock_1_out));
  Demultiplexer #(.select(4), .width(8), .tristate("true")) demultiplexer_1 (
    .out0(demultiplexer_1_out0), .out1(demultiplexer_1_out1), .out2(demultiplexer_1_out2),
    .out3(demultiplexer_1_out3), .out4(demultiplexer_1_out4), .out5(demultiplexer_1_out5),
    .out6(demultiplexer_1_out6), .out7(demultiplexer_1_out7), .out8(demultiplexer_1_out8),
    .out9(demultiplexer_1_out9), .out10(demultiplexer_1_out10), .out11(demultiplexer_1_out11),
    .out12(demultiplexer_1_out12), .out13(demultiplexer_1_out13), .out14(demultiplexer_1_out14),
    .out15(demultiplexer_1_out15), .in(valln), .sel(Selec_rd), .en(regW));
  Demultiplexer #(.select(4), .tristate("true")) demultiplexer_2 (
    .out0(demultiplexer_2_out0), .out1(demultiplexer_2_out1), .out2(demultiplexer_2_out2),
    .out3(demultiplexer_2_out3), .out4(demultiplexer_2_out4), .out5(demultiplexer_2_out5),
    .out6(demultiplexer_2_out6), .out7(demultiplexer_2_out7), .out8(demultiplexer_2_out8),
    .out9(demultiplexer_2_out9), .out10(demultiplexer_2_out10), .out11(demultiplexer_2_out11),
    .out12(demultiplexer_2_out12), .out13(demultiplexer_2_out13), .out14(demultiplexer_2_out14),
    .out15(demultiplexer_2_out15), .in(clock_1_out), .sel(Selec_rd), .en(regW));
  Register u_r16 (.D(demultiplexer_1_out15), .Q(R16), .clk(demultiplexer_2_out15), .clr(Reset));  // open: en
  Register u_r14 (.D(demultiplexer_1_out13), .Q(R14), .clk(demultiplexer_2_out13), .clr(Reset));  // open: en
  Register u_r15 (.D(demultiplexer_1_out14), .Q(R15), .clk(demultiplexer_2_out14), .clr(Reset));  // open: en
  Register u_r12 (.D(demultiplexer_1_out11), .Q(R12), .clk(demultiplexer_2_out11), .clr(Reset));  // open: en
  Register u_r13 (.D(demultiplexer_1_out12), .Q(R13), .clk(demultiplexer_2_out12), .clr(Reset));  // open: en
  Register u_r11 (.D(demultiplexer_1_out10), .Q(R11), .clk(demultiplexer_2_out10), .clr(Reset));  // open: en
  Register u_r9 (.D(demultiplexer_1_out8), .Q(R9), .clk(demultiplexer_2_out8), .clr(Reset));  // open: en
  Register u_r10 (.D(demultiplexer_1_out9), .Q(R10), .clk(demultiplexer_2_out9), .clr(Reset));  // open: en
  Register u_r8 (.D(demultiplexer_1_out7), .Q(R8), .clk(demultiplexer_2_out7), .clr(Reset));  // open: en
  Register u_r6 (.D(demultiplexer_1_out5), .Q(R6), .clk(demultiplexer_2_out5));  // open: en, clr
  Register u_r7 (.D(demultiplexer_1_out6), .Q(R7), .clk(demultiplexer_2_out6), .clr(Reset));  // open: en
  Register u_r4 (.D(demultiplexer_1_out3), .Q(R4), .clk(demultiplexer_2_out3), .clr(Reset));  // open: en
  Register u_r5 (.D(demultiplexer_1_out4), .Q(R5), .clk(demultiplexer_2_out4), .clr(Reset));  // open: en
  Register u_r3 (.D(demultiplexer_1_out2), .Q(R3), .clk(demultiplexer_2_out2), .clr(Reset));  // open: en
  Register u_r1 (.D(demultiplexer_1_out0), .Q(R1), .clk(demultiplexer_2_out0), .clr(Reset));  // open: en
  Register u_r2 (.D(demultiplexer_1_out1), .Q(R2), .clk(demultiplexer_2_out1), .clr(Reset));  // open: en
  Multiplexer #(.select(4), .width(8)) multiplexer_1 (
    .in1(R1), .in2(R2), .in3(R4), .in4(R5), .in5(R6), .in6(R7), .in7(R8), .in8(R9), .in9(R10), .in10(R11),
    .in11(R12), .in12(R13), .in13(R14), .in14(R15), .in15(R16), .out(Rt), .sel(Selc_rt));  // open: in0, en
  Multiplexer #(.select(4), .width(8)) multiplexer_2 (
    .in0(R1), .in1(R2), .in2(R3), .in3(R4), .in4(R5), .in5(R6), .in6(R7), .in7(R8), .in8(R9), .in9(R10),
    .in10(R11), .in11(R12), .in12(R13), .in13(R14), .in14(R15), .in15(R16), .out(Rs), .sel(Selec_rs));  // open: en
endmodule

module SelecteurReg (
  input  [2:0] rd_rs,
  input  [2:0] rs_rt,
  input  [2:0] rt,
  input  IsJMP,
  output [2:0] rd,
  output [2:0] rs,
  output [2:0] rt_2
);
endmodule
