// Logisim project massive_octo_computing_machine.circ as structural Verilog
module decodeur_instruction (
  input  [3:0] in_1,
  output regWrite,
  output isJump,
  output isLoad,
  output isUAL,
  output [2:0] out_6
);

  wire and_1_out, not_2_out, or_1_out, or_2_out;

  and and_1 (and_1_out, in_1[1], ~in_1[0]);  // AND_Gate
  not not_1 (isUAL, in_1[3]);
  or or_1 (or_1_out, in_1[0], in_1[1], in_1[2]);
  not not_2 (not_2_out, in_1[3]);
  or or_2 (or_2_out, ~in_1[2], ~in_1[1], and_1_out);  // OR_Gate
  and and_2 (regWrite, or_1_out, not_2_out);
  and and_3 (isJump, in_1[3], or_2_out);
  and and_4 (isLoad, in_1[0], in_1[1], in_1[2], in_1[3]);
  and and_5 (out_6[0], in_1[0], isUAL);
  and and_6 (out_6[1], in_1[1], isUAL);
  and and_7 (out_6[2], in_1[2], isUAL);

  // Notes on the sheet:
  //   abcd
endmodule
